// Logisim project FPA.circ as structural Verilog
module exponent_differentiator (
  input  [8:0] Ea,
  input  [8:0] Eb,
  output out_3,
  output [4:0] SFT,
  output FULL_SFT
);

  wire subtractor_1_bout;
  wire [8:0] EXP_DEF, negator_1_out;
  wire [8:6] ABS_EXP_DEF;

  Subtractor #(.width(9)) subtractor_1 (.a(Ea), .b(Eb), .out(EXP_DEF), .bout(subtractor_1_bout));  // open: bin
  not not_1 (out_3, subtractor_1_bout);
  Negator #(.width(9)) negator_1 (.in(EXP_DEF), .out(negator_1_out));
  Multiplexer #(.width(9), .enable("false")) multiplexer_1 (
    .in0(negator_1_out), .in1(EXP_DEF), .out({ABS_EXP_DEF, FULL_SFT, SFT}), .sel(out_3));

  // Other names for the same wires on the sheet: ABS_EXP_DEF[5:0] = {FULL_SFT, SFT}; Smaller_Exponent = out_3
endmodule

module shifter (
  input  [31:0] significant,
  input  [4:0] SFT,
  input  L_R_SFT,
  input  FULL_SFT,
  output [31:0] out_5
);

  wire [31:0] LFT_SFT, RHT_SFT;

  Shifter #(.width(32), .shift("lr")) shifter_1 (.in(significant), .\dist (SFT), .out(RHT_SFT));
  Shifter #(.width(32)) shifter_2 (.in(significant), .\dist (SFT), .out(LFT_SFT));
  Multiplexer #(.select(2), .width(32), .enable("false")) multiplexer_1 (
    .in0(LFT_SFT), .in1(RHT_SFT), .in2({32{1'b0}}), .in3({32{1'b0}}), .out(out_5), .sel({FULL_SFT, L_R_SFT}));
endmodule

module significant_formatter (
  input  [21:0] in_1,
  output [31:0] out_2
);


  assign out_2 = {in_1, {10{1'b0}}};
endmodule
